// Logisim project Matriz leds conecta 4.circ as structural Verilog
module main (
);

  wire _1_out, _2_out, _3_out, _4_out, _5_out, _6_out, _7_out, matriz_1_gana, pantalla_1_entrada,
       pantalla_1_lock, pantalla_1_parar, Reset_out, turno_1_invalida;
  wire [1:0] matriz_1_lock_reset, turno_1_jugador;
  wire [6:0] columna_1_out_7, pantalla_1_valor;
  wire [11:0] columna_1_out_24, columna_2_out_24, columna_3_out_24, columna_4_out_24, columna_5_out_24,
       columna_6_out_24, columna_7_out_24;

  Turno turno_1 (
    .c1(_1_out), .c2(_2_out), .c3(_3_out), .c4(_4_out), .c5(_5_out), .c6(_6_out), .c7(_7_out),
    .Jugador(turno_1_jugador), .l1(columna_1_out_7), .Invalida(turno_1_invalida));
  Button Reset (.out(Reset_out));
  Button _2 (.out(_2_out));
  Button _1 (.out(_1_out));
  Borde borde_1 ();
  Columna columna_1 (
    .Entrada(_1_out), .Clock(1'b1), .Jugador(turno_1_jugador), .out_24(columna_1_out_24),
    .out_7(columna_1_out_7[0]), .L_R(matriz_1_lock_reset));  // open: out_5, out_6, out_8, out_9, out_10, out_11, out_12, out_13, out_14, out_15, out_16, out_17, out_18, out_19, out_20, out_21, out_22, out_23
  Columna columna_2 (
    .Entrada(_3_out), .Clock(1'b1), .Jugador(turno_1_jugador), .out_24(columna_2_out_24),
    .out_7(columna_1_out_7[2]), .L_R(matriz_1_lock_reset));  // open: out_5, out_6, out_8, out_9, out_10, out_11, out_12, out_13, out_14, out_15, out_16, out_17, out_18, out_19, out_20, out_21, out_22, out_23
  Columna columna_3 (
    .Entrada(_2_out), .Clock(1'b1), .Jugador(turno_1_jugador), .out_24(columna_3_out_24),
    .out_7(columna_1_out_7[1]), .L_R(matriz_1_lock_reset));  // open: out_5, out_6, out_8, out_9, out_10, out_11, out_12, out_13, out_14, out_15, out_16, out_17, out_18, out_19, out_20, out_21, out_22, out_23
  // RGBLed #(.multibit("true")) rgbled_1: pin names not known
  // RGBLed #(.multibit("true")) rgbled_2: pin names not known; wires that end beside it: turno_1_jugador
  // RGBLed #(.multibit("true")) rgbled_3: pin names not known
  // RGBLed #(.multibit("true")) rgbled_4: pin names not known
  // RGBLed #(.multibit("true")) rgbled_5: pin names not known
  // RGBLed #(.multibit("true")) rgbled_6: pin names not known
  // RGBLed #(.multibit("true")) rgbled_7: pin names not known
  // RGBLed #(.multibit("true")) rgbled_8: pin names not known
  // RGBLed #(.multibit("true")) rgbled_9: pin names not known
  // RGBLed #(.multibit("true")) rgbled_10: pin names not known
  // RGBLed #(.multibit("true")) rgbled_11: pin names not known
  // RGBLed #(.multibit("true")) rgbled_12: pin names not known
  // RGBLed #(.multibit("true")) rgbled_13: pin names not known
  // RGBLed #(.multibit("true")) rgbled_14: pin names not known
  // RGBLed #(.multibit("true")) rgbled_15: pin names not known
  // RGBLed #(.multibit("true")) rgbled_16: pin names not known
  // RGBLed #(.multibit("true")) rgbled_17: pin names not known
  // RGBLed #(.multibit("true")) rgbled_18: pin names not known
  Button _5 (.out(_5_out));
  Button _3 (.out(_3_out));
  Button _4 (.out(_4_out));
  Columna columna_4 (
    .Entrada(_5_out), .Clock(1'b1), .Jugador(turno_1_jugador), .out_24(columna_4_out_24),
    .out_7(columna_1_out_7[4]), .L_R(matriz_1_lock_reset));  // open: out_5, out_6, out_8, out_9, out_10, out_11, out_12, out_13, out_14, out_15, out_16, out_17, out_18, out_19, out_20, out_21, out_22, out_23
  Columna columna_5 (
    .Entrada(_4_out), .Clock(1'b1), .Jugador(turno_1_jugador), .out_24(columna_5_out_24),
    .out_7(columna_1_out_7[3]), .L_R(matriz_1_lock_reset));  // open: out_5, out_6, out_8, out_9, out_10, out_11, out_12, out_13, out_14, out_15, out_16, out_17, out_18, out_19, out_20, out_21, out_22, out_23
  // RGBLed #(.multibit("true")) rgbled_19: pin names not known
  // RGBLed #(.multibit("true")) rgbled_20: pin names not known
  // RGBLed #(.multibit("true")) rgbled_21: pin names not known
  // RGBLed #(.multibit("true")) rgbled_22: pin names not known
  // RGBLed #(.multibit("true")) rgbled_23: pin names not known
  // RGBLed #(.multibit("true")) rgbled_24: pin names not known
  // RGBLed #(.multibit("true")) rgbled_25: pin names not known
  // RGBLed #(.multibit("true")) rgbled_26: pin names not known
  // RGBLed #(.multibit("true")) rgbled_27: pin names not known
  // RGBLed #(.multibit("true")) rgbled_28: pin names not known
  // RGBLed #(.multibit("true")) rgbled_29: pin names not known
  // RGBLed #(.multibit("true")) rgbled_30: pin names not known
  Matriz matriz_1 (
    .c1(columna_3_out_24), .c2(columna_2_out_24), .c3(columna_5_out_24), .c4(columna_4_out_24),
    .c5(columna_7_out_24), .c6(columna_6_out_24), .c0(columna_1_out_24), .Clock(1'b1), .Gana(matriz_1_gana),
    .Lock_Reset(matriz_1_lock_reset), .Lock(pantalla_1_lock), .Reset(Reset_out));
  Button _6 (.out(_6_out));
  Button _7 (.out(_7_out));
  Borde borde_2 ();
  Borde borde_3 ();
  Columna columna_6 (
    .Entrada(_7_out), .Clock(1'b1), .Jugador(turno_1_jugador), .out_24(columna_6_out_24),
    .out_7(columna_1_out_7[6]), .L_R(matriz_1_lock_reset));  // open: out_5, out_6, out_8, out_9, out_10, out_11, out_12, out_13, out_14, out_15, out_16, out_17, out_18, out_19, out_20, out_21, out_22, out_23
  Columna columna_7 (
    .Entrada(_6_out), .Clock(1'b1), .Jugador(turno_1_jugador), .out_24(columna_7_out_24),
    .out_7(columna_1_out_7[5]), .L_R(matriz_1_lock_reset));  // open: out_5, out_6, out_8, out_9, out_10, out_11, out_12, out_13, out_14, out_15, out_16, out_17, out_18, out_19, out_20, out_21, out_22, out_23
  // RGBLed #(.multibit("true")) rgbled_31: pin names not known
  // RGBLed #(.multibit("true")) rgbled_32: pin names not known; wires that end beside it: _7_out
  // RGBLed #(.multibit("true")) rgbled_33: pin names not known
  // RGBLed #(.multibit("true")) rgbled_34: pin names not known
  // RGBLed #(.multibit("true")) rgbled_35: pin names not known
  // RGBLed #(.multibit("true")) rgbled_36: pin names not known
  // RGBLed #(.multibit("true")) rgbled_37: pin names not known
  // RGBLed #(.multibit("true")) rgbled_38: pin names not known
  // RGBLed #(.multibit("true")) rgbled_39: pin names not known
  // RGBLed #(.multibit("true")) rgbled_40: pin names not known
  // RGBLed #(.multibit("true")) rgbled_41: pin names not known
  // RGBLed #(.multibit("true")) rgbled_42: pin names not known
  pantalla pantalla_1 (
    .Jugador(turno_1_jugador), .valor(pantalla_1_valor), .entrada(pantalla_1_entrada),
    .parar(pantalla_1_parar), .Gana(matriz_1_gana), .Invalida(turno_1_invalida), .Lock(pantalla_1_lock),
    .Clear(matriz_1_lock_reset[1]));
  TTY #(.rows(1), .cols(23)) tty_1 (
    .data(pantalla_1_valor), .clk(pantalla_1_entrada), .we(pantalla_1_parar), .clr(matriz_1_lock_reset[1]));
endmodule

module Columna (
  input  Entrada,
  input  Clock,
  input  [1:0] Jugador,
  input  [1:0] L_R,
  output [7:0] out_5,
  output [7:0] out_6,
  output out_7,
  output [7:0] out_8,
  output [7:0] out_9,
  output [7:0] out_10,
  output [7:0] out_11,
  output [7:0] out_12,
  output [7:0] out_13,
  output [7:0] out_14,
  output [7:0] out_15,
  output [7:0] out_16,
  output [7:0] out_17,
  output [7:0] out_18,
  output [7:0] out_19,
  output [7:0] out_20,
  output [7:0] out_21,
  output [7:0] out_22,
  output [7:0] out_23,
  output [11:0] out_24
);

  wire and_1_out, and_2_out, comparator_1_lt, counter_1_carry, counter_1_q, counter_2_carry,
       demultiplexer_1_out0, demultiplexer_1_out1, demultiplexer_1_out2, demultiplexer_1_out3,
       demultiplexer_1_out4, demultiplexer_1_out5, not_1_out, not_2_out, not_3_out, On;
  wire [0:0] and_3_out;
  wire [1:0] demultiplexer_2_out0, demultiplexer_2_out1, demultiplexer_2_out2, demultiplexer_2_out3,
       demultiplexer_2_out4, demultiplexer_2_out5;
  wire [2:0] ocupados, posix;

  Demultiplexer #(.select(3), .enable("false")) demultiplexer_1 (
    .out0(demultiplexer_1_out0), .out1(demultiplexer_1_out1), .out2(demultiplexer_1_out2),
    .out3(demultiplexer_1_out3), .out4(demultiplexer_1_out4), .out5(demultiplexer_1_out5), .in(On),
    .sel(posix));  // open: out6, out7
  Demultiplexer #(.select(3), .width(2), .enable("false")) demultiplexer_2 (
    .out0(demultiplexer_2_out0), .out1(demultiplexer_2_out1), .out2(demultiplexer_2_out2),
    .out3(demultiplexer_2_out3), .out4(demultiplexer_2_out4), .out5(demultiplexer_2_out5), .in(Jugador),
    .sel(posix));  // open: out6, out7
  not not_1 (not_1_out, L_R[0]);
  Register #(.width(2), .Select("low")) _1 (
    .D(demultiplexer_2_out0), .en(not_1_out), .Q(out_24[1:0]), .clk(demultiplexer_1_out0), .clr(L_R[1]));
  Register #(.width(2), .trigger("high"), .Select("low")) _2 (
    .D(demultiplexer_2_out1), .en(not_1_out), .Q(out_24[3:2]), .clk(demultiplexer_1_out1), .clr(L_R[1]));
  Register #(.width(2), .trigger("high"), .Select("low")) _3 (
    .D(demultiplexer_2_out2), .en(not_1_out), .Q(out_24[5:4]), .clk(demultiplexer_1_out2), .clr(L_R[1]));
  Register #(.width(2), .trigger("high"), .Select("low")) _4 (
    .D(demultiplexer_2_out3), .en(not_1_out), .Q(out_24[7:6]), .clk(demultiplexer_1_out3), .clr(L_R[1]));
  Register #(.width(2), .trigger("high"), .Select("low")) _5 (
    .D(demultiplexer_2_out4), .en(not_1_out), .Q(out_24[9:8]), .clk(demultiplexer_1_out4), .clr(L_R[1]));
  Register #(.width(2), .trigger("high"), .Select("low")) _6 (
    .D(demultiplexer_2_out5), .en(not_1_out), .Q(out_24[11:10]), .clk(demultiplexer_1_out5), .clr(L_R[1]));
  Color color_1 (.Jugador(out_24[1:0]), .out_2({out_5, out_6, out_8}));
  Color color_2 (.Jugador(out_24[3:2]), .out_2({out_9, out_10, out_11}));
  Color color_3 (.Jugador(out_24[5:4]), .out_2({out_12, out_13, out_14}));
  Color color_4 (.Jugador(out_24[7:6]), .out_2({out_15, out_16, out_17}));
  Color color_5 (.Jugador(out_24[9:8]), .out_2({out_18, out_19, out_20}));
  Color color_6 (.Jugador(out_24[11:10]), .out_2({out_21, out_22, out_23}));
  Subtractor #(.width(3)) subtractor_1 (.a(3'b101), .b(ocupados), .out(posix));  // open: bin, bout
  Comparator #(.width(3), .mode("unsigned")) comparator_1 (
    .a(ocupados), .b(3'b110), .eq(out_7), .lt(comparator_1_lt));  // open: gt
  Counter #(.width(1), .max('h1), .ongoal("continue"), .trigger("falling")) counter_1 (
    .D(Entrada), .Q(counter_1_q), .carry(counter_1_carry), .clk(Entrada), .clr(and_1_out));  // open: load, count, preset, down
  and and_1 (and_1_out, Clock, counter_1_carry);
  and and_2 (and_2_out, Clock, and_3_out[0]);
  and and_3 (and_3_out[0], comparator_1_lt, counter_1_q);
  and and_4 (On, and_2_out, not_2_out);
  not not_2 (not_2_out, L_R[0]);
  Counter #(.width(3), .max('h6), .trigger("falling")) counter_2 (
    .D({2'b00, and_3_out[0]}), .count(not_3_out), .Q(ocupados), .carry(counter_2_carry), .clk(On),
    .clr(L_R[1]));  // open: load, preset, down
  not not_3 (not_3_out, counter_2_carry);

  // Other names for the same wires on the sheet: Lock = L_R[0]; Reset = L_R[1]
endmodule

module Matriz (
  input  [11:0] c1,
  input  [11:0] c2,
  input  [11:0] c3,
  input  [11:0] c4,
  input  [11:0] c5,
  input  [11:0] c6,
  input  [11:0] c0,
  input  Clock,
  input  Lock,
  input  Reset,
  output [1:0] Lock_Reset,
  output Gana
);

  wire diagonal_1_out_43, horizontal_1_out_43, vertical_1_out_43;
  wire [1:0] _01_q, _03_q, _04_q, _05_q, _06_q, _11_q, _13_q, _14_q, _15_q, _16_q, _21_q, _23_q, _24_q,
       _25_q, _26_q, _31_q, _33_q, _34_q, _35_q, _36_q, _41_q, _43_q, _44_q, _45_q, _46_q, _51_q, _53_q,
       _54_q, _55_q, _56_q, register_1_q, register_2_q, register_3_q, register_4_q, register_5_q,
       register_6_q, register_7_q, register_8_q, register_9_q, register_10_q, register_11_q, register_12_q;

  Vertical vertical_1 (
    ._00(register_6_q), ._10(register_5_q), ._20(register_4_q), ._30(register_3_q), ._40(register_2_q),
    ._50(register_1_q), ._01(_51_q), ._11(_41_q), ._21(_31_q), ._31(_21_q), ._41(_11_q), ._51(_01_q),
    ._02(register_12_q), ._12(register_11_q), ._22(register_10_q), ._32(register_9_q), ._42(register_8_q),
    ._52(register_7_q), ._03(_53_q), ._13(_43_q), ._23(_33_q), ._33(_23_q), ._43(_13_q), ._53(_03_q),
    ._04(_54_q), ._14(_44_q), ._24(_34_q), ._34(_24_q), ._44(_14_q), ._54(_04_q), ._05(_55_q), ._15(_45_q),
    ._25(_35_q), ._35(_25_q), ._45(_15_q), ._55(_05_q), ._06(_56_q), ._16(_46_q), ._26(_36_q), ._36(_26_q),
    ._46(_16_q), ._56(_06_q), .out_43(vertical_1_out_43));
  Register #(.width(2), .trigger("high"), .Select("low")) register_1 (
    .D(c0[1:0]), .Q(register_1_q), .clk(Clock));  // open: en, clr
  Register #(.width(2), .trigger("high"), .Select("low")) register_2 (
    .D(c0[3:2]), .Q(register_2_q), .clk(Clock));  // open: en, clr
  Register #(.width(2), .trigger("high"), .Select("low")) register_3 (
    .D(c0[5:4]), .Q(register_3_q), .clk(Clock));  // open: en, clr
  Register #(.width(2), .trigger("high"), .Select("low")) register_4 (
    .D(c0[7:6]), .Q(register_4_q), .clk(Clock));  // open: en, clr
  Register #(.width(2), .trigger("high"), .Select("low")) register_5 (
    .D(c0[9:8]), .Q(register_5_q), .clk(Clock));  // open: en, clr
  Register #(.width(2), .trigger("high"), .Select("low")) register_6 (
    .D(c0[11:10]), .Q(register_6_q), .clk(Clock));  // open: en, clr
  or or_1 (Gana, vertical_1_out_43, horizontal_1_out_43, diagonal_1_out_43);
  or or_2 (Lock_Reset[0], Lock, Gana);
  Register #(.width(2), .trigger("high"), .Select("low")) _01 (.D(c1[1:0]), .Q(_01_q), .clk(Clock));  // open: en, clr
  Register #(.width(2), .trigger("high"), .Select("low")) _11 (.D(c1[3:2]), .Q(_11_q), .clk(Clock));  // open: en, clr
  Register #(.width(2), .trigger("high"), .Select("low")) _21 (.D(c1[5:4]), .Q(_21_q), .clk(Clock));  // open: en, clr
  Register #(.width(2), .trigger("high"), .Select("low")) _31 (.D(c1[7:6]), .Q(_31_q), .clk(Clock));  // open: en, clr
  Register #(.width(2), .trigger("high"), .Select("low")) _41 (.D(c1[9:8]), .Q(_41_q), .clk(Clock));  // open: en, clr
  Register #(.width(2), .trigger("high"), .Select("low")) _51 (.D(c1[11:10]), .Q(_51_q), .clk(Clock));  // open: en, clr
  Register #(.width(2), .trigger("high"), .Select("low")) register_7 (
    .D(c2[1:0]), .Q(register_7_q), .clk(Clock));  // open: en, clr
  Register #(.width(2), .trigger("high"), .Select("low")) register_8 (
    .D(c2[3:2]), .Q(register_8_q), .clk(Clock));  // open: en, clr
  Register #(.width(2), .trigger("high"), .Select("low")) register_9 (
    .D(c2[5:4]), .Q(register_9_q), .clk(Clock));  // open: en, clr
  Register #(.width(2), .trigger("high"), .Select("low")) register_10 (
    .D(c2[7:6]), .Q(register_10_q), .clk(Clock));  // open: en, clr
  Register #(.width(2), .trigger("high"), .Select("low")) register_11 (
    .D(c2[9:8]), .Q(register_11_q), .clk(Clock));  // open: en, clr
  Register #(.width(2), .trigger("high"), .Select("low")) register_12 (
    .D(c2[11:10]), .Q(register_12_q), .clk(Clock));  // open: en, clr
  Register #(.width(2), .trigger("high"), .Select("low")) _03 (.D(c3[1:0]), .Q(_03_q), .clk(Clock));  // open: en, clr
  Register #(.width(2), .trigger("high"), .Select("low")) _13 (.D(c3[3:2]), .Q(_13_q), .clk(Clock));  // open: en, clr
  Register #(.width(2), .trigger("high"), .Select("low")) _23 (.D(c3[5:4]), .Q(_23_q), .clk(Clock));  // open: en, clr
  Register #(.width(2), .trigger("high"), .Select("low")) _33 (.D(c3[7:6]), .Q(_33_q), .clk(Clock));  // open: en, clr
  Register #(.width(2), .trigger("high"), .Select("low")) _43 (.D(c3[9:8]), .Q(_43_q), .clk(Clock));  // open: en, clr
  Register #(.width(2), .trigger("high"), .Select("low")) _53 (.D(c3[11:10]), .Q(_53_q), .clk(Clock));  // open: en, clr
  Horizontal horizontal_1 (
    ._00(register_6_q), ._01(_51_q), ._02(register_12_q), ._03(_53_q), ._04(_54_q), ._05(_55_q), ._06(_56_q),
    ._10(register_5_q), ._11(_41_q), ._12(register_11_q), ._13(_43_q), ._14(_44_q), ._15(_45_q), ._16(_46_q),
    ._20(register_4_q), ._21(_31_q), ._22(register_10_q), ._23(_33_q), ._24(_34_q), ._25(_35_q), ._26(_36_q),
    ._30(register_3_q), ._31(_21_q), ._32(register_9_q), ._33(_23_q), ._34(_24_q), ._35(_25_q), ._36(_26_q),
    ._40(register_2_q), ._41(_11_q), ._42(register_8_q), ._43(_13_q), ._44(_14_q), ._45(_15_q), ._46(_16_q),
    ._50(register_1_q), ._51(_01_q), ._52(register_7_q), ._53(_03_q), ._54(_04_q), ._55(_05_q), ._56(_06_q),
    .out_43(horizontal_1_out_43));
  Register #(.width(2), .trigger("high"), .Select("low")) _04 (.D(c4[1:0]), .Q(_04_q), .clk(Clock));  // open: en, clr
  Register #(.width(2), .trigger("high"), .Select("low")) _14 (.D(c4[3:2]), .Q(_14_q), .clk(Clock));  // open: en, clr
  Register #(.width(2), .trigger("high"), .Select("low")) _24 (.D(c4[5:4]), .Q(_24_q), .clk(Clock));  // open: en, clr
  Register #(.width(2), .trigger("high"), .Select("low")) _34 (.D(c4[7:6]), .Q(_34_q), .clk(Clock));  // open: en, clr
  Register #(.width(2), .trigger("high"), .Select("low")) _44 (.D(c4[9:8]), .Q(_44_q), .clk(Clock));  // open: en, clr
  Register #(.width(2), .trigger("high"), .Select("low")) _54 (.D(c4[11:10]), .Q(_54_q), .clk(Clock));  // open: en, clr
  Register #(.width(2), .trigger("high"), .Select("low")) _05 (.D(c5[1:0]), .Q(_05_q), .clk(Clock));  // open: en, clr
  Register #(.width(2), .trigger("high"), .Select("low")) _15 (.D(c5[3:2]), .Q(_15_q), .clk(Clock));  // open: en, clr
  Register #(.width(2), .trigger("high"), .Select("low")) _25 (.D(c5[5:4]), .Q(_25_q), .clk(Clock));  // open: en, clr
  Register #(.width(2), .trigger("high"), .Select("low")) _35 (.D(c5[7:6]), .Q(_35_q), .clk(Clock));  // open: en, clr
  Register #(.width(2), .trigger("high"), .Select("low")) _45 (.D(c5[9:8]), .Q(_45_q), .clk(Clock));  // open: en, clr
  Register #(.width(2), .trigger("high"), .Select("low")) _55 (.D(c5[11:10]), .Q(_55_q), .clk(Clock));  // open: en, clr
  Register #(.width(2), .trigger("high"), .Select("low")) _06 (.D(c6[1:0]), .Q(_06_q), .clk(Clock));  // open: en, clr
  Register #(.width(2), .trigger("high"), .Select("low")) _16 (.D(c6[3:2]), .Q(_16_q), .clk(Clock));  // open: en, clr
  Register #(.width(2), .trigger("high"), .Select("low")) _26 (.D(c6[5:4]), .Q(_26_q), .clk(Clock));  // open: en, clr
  Register #(.width(2), .trigger("high"), .Select("low")) _36 (.D(c6[7:6]), .Q(_36_q), .clk(Clock));  // open: en, clr
  Register #(.width(2), .trigger("high"), .Select("low")) _46 (.D(c6[9:8]), .Q(_46_q), .clk(Clock));  // open: en, clr
  Register #(.width(2), .trigger("high"), .Select("low")) _56 (.D(c6[11:10]), .Q(_56_q), .clk(Clock));  // open: en, clr
  Diagonal diagonal_1 (
    ._00(register_1_q), ._20(register_3_q), ._40(register_5_q), ._01(_01_q), ._21(_21_q), ._41(_41_q),
    ._02(register_7_q), ._22(register_9_q), ._42(register_11_q), ._03(_03_q), ._23(_23_q), ._43(_43_q),
    ._04(_04_q), ._24(_24_q), ._44(_44_q), ._05(_05_q), ._25(_25_q), ._45(_45_q), ._06(_06_q), ._26(_26_q),
    ._46(_46_q), ._10(register_2_q), ._30(register_4_q), ._50(register_6_q), ._11(_11_q), ._31(_31_q),
    ._51(_51_q), ._12(register_8_q), ._32(register_10_q), ._52(register_12_q), ._13(_13_q), ._33(_33_q),
    ._53(_53_q), ._14(_14_q), ._34(_34_q), ._54(_54_q), ._15(_15_q), ._35(_35_q), ._55(_55_q), ._16(_16_q),
    ._36(_36_q), ._56(_56_q), .out_43(diagonal_1_out_43));

  assign Lock_Reset[1] = Reset;
endmodule

module Vertical (
  input  [1:0] _00,
  input  [1:0] _10,
  input  [1:0] _20,
  input  [1:0] _30,
  input  [1:0] _40,
  input  [1:0] _50,
  input  [1:0] _01,
  input  [1:0] _11,
  input  [1:0] _21,
  input  [1:0] _31,
  input  [1:0] _41,
  input  [1:0] _51,
  input  [1:0] _02,
  input  [1:0] _12,
  input  [1:0] _22,
  input  [1:0] _32,
  input  [1:0] _42,
  input  [1:0] _52,
  input  [1:0] _03,
  input  [1:0] _13,
  input  [1:0] _23,
  input  [1:0] _33,
  input  [1:0] _43,
  input  [1:0] _53,
  input  [1:0] _04,
  input  [1:0] _14,
  input  [1:0] _24,
  input  [1:0] _34,
  input  [1:0] _44,
  input  [1:0] _54,
  input  [1:0] _05,
  input  [1:0] _15,
  input  [1:0] _25,
  input  [1:0] _35,
  input  [1:0] _45,
  input  [1:0] _55,
  input  [1:0] _06,
  input  [1:0] _16,
  input  [1:0] _26,
  input  [1:0] _36,
  input  [1:0] _46,
  input  [1:0] _56,
  output out_43
);

  wire comparator_1_eq, comparator_2_eq, comparator_3_eq, comparator_4_eq, comparator_5_eq, comparator_6_eq,
       comparator_7_eq, comparator_8_eq, comparator_9_eq, comparator_10_eq, comparator_11_eq,
       comparator_12_eq, comparator_13_eq, comparator_14_eq, or_8_out, or_9_out, or_10_out, or_11_out,
       or_12_out, or_13_out, or_14_out;
  wire [1:0] and_1_out, and_2_out, and_3_out, and_4_out, and_5_out, and_6_out, and_7_out, and_8_out,
       and_9_out, and_10_out, and_11_out, and_12_out, and_13_out, and_14_out, and_15_out, and_16_out,
       and_17_out, and_18_out, and_19_out, and_20_out, and_21_out, or_1_out, or_2_out, or_3_out, or_4_out,
       or_5_out, or_6_out, or_7_out;

  assign and_1_out = _00 & _10 & _20 & _30;  // AND_Gate and_1, 2 bits wide
  assign and_2_out = _10 & _20 & _30 & _40;  // AND_Gate and_2, 2 bits wide
  assign and_3_out = _20 & _30 & _40 & _50;  // AND_Gate and_3, 2 bits wide
  assign and_4_out = _01 & _11 & _21 & _31;  // AND_Gate and_4, 2 bits wide
  assign and_5_out = _11 & _21 & _31 & _41;  // AND_Gate and_5, 2 bits wide
  assign and_6_out = _21 & _31 & _41 & _51;  // AND_Gate and_6, 2 bits wide
  assign and_7_out = _02 & _12 & _22 & _32;  // AND_Gate and_7, 2 bits wide
  assign and_8_out = _12 & _22 & _32 & _42;  // AND_Gate and_8, 2 bits wide
  assign and_9_out = _22 & _32 & _42 & _52;  // AND_Gate and_9, 2 bits wide
  assign and_10_out = _03 & _13 & _23 & _33;  // AND_Gate and_10, 2 bits wide
  assign and_11_out = _13 & _23 & _33 & _43;  // AND_Gate and_11, 2 bits wide
  assign and_12_out = _23 & _33 & _43 & _53;  // AND_Gate and_12, 2 bits wide
  assign and_13_out = _04 & _14 & _24 & _34;  // AND_Gate and_13, 2 bits wide
  assign and_14_out = _14 & _24 & _34 & _44;  // AND_Gate and_14, 2 bits wide
  assign and_15_out = _24 & _34 & _44 & _54;  // AND_Gate and_15, 2 bits wide
  assign and_16_out = _05 & _15 & _25 & _35;  // AND_Gate and_16, 2 bits wide
  assign and_17_out = _15 & _25 & _35 & _45;  // AND_Gate and_17, 2 bits wide
  assign and_18_out = _25 & _35 & _45 & _55;  // AND_Gate and_18, 2 bits wide
  assign and_19_out = _06 & _16 & _26 & _36;  // AND_Gate and_19, 2 bits wide
  assign and_20_out = _16 & _26 & _36 & _46;  // AND_Gate and_20, 2 bits wide
  assign and_21_out = _26 & _36 & _46 & _56;  // AND_Gate and_21, 2 bits wide
  assign or_1_out = and_1_out | and_2_out | and_3_out;  // OR_Gate or_1, 2 bits wide
  assign or_2_out = and_4_out | and_5_out | and_6_out;  // OR_Gate or_2, 2 bits wide
  assign or_3_out = and_7_out | and_8_out | and_9_out;  // OR_Gate or_3, 2 bits wide
  assign or_4_out = and_10_out | and_11_out | and_12_out;  // OR_Gate or_4, 2 bits wide
  assign or_5_out = and_13_out | and_14_out | and_15_out;  // OR_Gate or_5, 2 bits wide
  assign or_6_out = and_16_out | and_17_out | and_18_out;  // OR_Gate or_6, 2 bits wide
  assign or_7_out = and_19_out | and_20_out | and_21_out;  // OR_Gate or_7, 2 bits wide
  Comparator #(.width(2), .mode("unsigned")) comparator_1 (
    .a(or_1_out), .b(2'b01), .eq(comparator_1_eq));  // open: gt, lt
  Comparator #(.width(2), .mode("unsigned")) comparator_2 (
    .a(or_1_out), .b(2'b10), .eq(comparator_2_eq));  // open: gt, lt
  Comparator #(.width(2), .mode("unsigned")) comparator_3 (
    .a(or_2_out), .b(2'b01), .eq(comparator_3_eq));  // open: gt, lt
  Comparator #(.width(2), .mode("unsigned")) comparator_4 (
    .a(or_2_out), .b(2'b10), .eq(comparator_4_eq));  // open: gt, lt
  Comparator #(.width(2), .mode("unsigned")) comparator_5 (
    .a(or_3_out), .b(2'b01), .eq(comparator_5_eq));  // open: gt, lt
  Comparator #(.width(2), .mode("unsigned")) comparator_6 (
    .a(or_3_out), .b(2'b10), .eq(comparator_6_eq));  // open: gt, lt
  Comparator #(.width(2), .mode("unsigned")) comparator_7 (
    .a(or_4_out), .b(2'b01), .eq(comparator_7_eq));  // open: gt, lt
  Comparator #(.width(2), .mode("unsigned")) comparator_8 (
    .a(or_4_out), .b(2'b10), .eq(comparator_8_eq));  // open: gt, lt
  Comparator #(.width(2), .mode("unsigned")) comparator_9 (
    .a(or_5_out), .b(2'b01), .eq(comparator_9_eq));  // open: gt, lt
  Comparator #(.width(2), .mode("unsigned")) comparator_10 (
    .a(or_5_out), .b(2'b10), .eq(comparator_10_eq));  // open: gt, lt
  Comparator #(.width(2), .mode("unsigned")) comparator_11 (
    .a(or_6_out), .b(2'b01), .eq(comparator_11_eq));  // open: gt, lt
  Comparator #(.width(2), .mode("unsigned")) comparator_12 (
    .a(or_6_out), .b(2'b10), .eq(comparator_12_eq));  // open: gt, lt
  Comparator #(.width(2), .mode("unsigned")) comparator_13 (
    .a(or_7_out), .b(2'b01), .eq(comparator_13_eq));  // open: gt, lt
  Comparator #(.width(2), .mode("unsigned")) comparator_14 (
    .a(or_7_out), .b(2'b10), .eq(comparator_14_eq));  // open: gt, lt
  or or_8 (or_8_out, comparator_1_eq, comparator_2_eq);
  or or_9 (or_9_out, comparator_3_eq, comparator_4_eq);
  or or_10 (or_10_out, comparator_5_eq, comparator_6_eq);
  or or_11 (or_11_out, comparator_7_eq, comparator_8_eq);
  or or_12 (or_12_out, comparator_9_eq, comparator_10_eq);
  or or_13 (or_13_out, comparator_11_eq, comparator_12_eq);
  or or_14 (or_14_out, comparator_13_eq, comparator_14_eq);
  or or_15 (out_43, or_8_out, or_9_out, or_10_out, or_11_out, or_12_out, or_13_out, or_14_out);
endmodule

module Horizontal (
  input  [1:0] _00,
  input  [1:0] _01,
  input  [1:0] _02,
  input  [1:0] _03,
  input  [1:0] _04,
  input  [1:0] _05,
  input  [1:0] _06,
  input  [1:0] _10,
  input  [1:0] _11,
  input  [1:0] _12,
  input  [1:0] _13,
  input  [1:0] _14,
  input  [1:0] _15,
  input  [1:0] _16,
  input  [1:0] _20,
  input  [1:0] _21,
  input  [1:0] _22,
  input  [1:0] _23,
  input  [1:0] _24,
  input  [1:0] _25,
  input  [1:0] _26,
  input  [1:0] _30,
  input  [1:0] _31,
  input  [1:0] _32,
  input  [1:0] _33,
  input  [1:0] _34,
  input  [1:0] _35,
  input  [1:0] _36,
  input  [1:0] _40,
  input  [1:0] _41,
  input  [1:0] _42,
  input  [1:0] _43,
  input  [1:0] _44,
  input  [1:0] _45,
  input  [1:0] _46,
  input  [1:0] _50,
  input  [1:0] _51,
  input  [1:0] _52,
  input  [1:0] _53,
  input  [1:0] _54,
  input  [1:0] _55,
  input  [1:0] _56,
  output out_43
);

  wire comparator_1_eq, comparator_2_eq, comparator_3_eq, comparator_4_eq, comparator_5_eq, comparator_6_eq,
       comparator_7_eq, comparator_8_eq, comparator_9_eq, comparator_10_eq, comparator_11_eq,
       comparator_12_eq, or_7_out, or_8_out, or_9_out, or_10_out, or_11_out, or_12_out;
  wire [1:0] and_1_out, and_2_out, and_3_out, and_4_out, and_5_out, and_6_out, and_7_out, and_8_out,
       and_9_out, and_10_out, and_11_out, and_12_out, and_13_out, and_14_out, and_15_out, and_16_out,
       and_17_out, and_18_out, and_19_out, and_20_out, and_21_out, and_22_out, and_23_out, and_24_out,
       or_1_out, or_2_out, or_3_out, or_4_out, or_5_out, or_6_out;

  assign and_1_out = _01 & _02 & _03 & _04;  // AND_Gate and_1, 2 bits wide
  assign and_2_out = _02 & _03 & _04 & _05;  // AND_Gate and_2, 2 bits wide
  assign and_3_out = _03 & _04 & _05 & _06;  // AND_Gate and_3, 2 bits wide
  assign and_4_out = _11 & _12 & _13 & _14;  // AND_Gate and_4, 2 bits wide
  assign and_5_out = _12 & _13 & _14 & _15;  // AND_Gate and_5, 2 bits wide
  assign and_6_out = _13 & _14 & _15 & _16;  // AND_Gate and_6, 2 bits wide
  assign and_7_out = _21 & _22 & _23 & _24;  // AND_Gate and_7, 2 bits wide
  assign and_8_out = _22 & _23 & _24 & _25;  // AND_Gate and_8, 2 bits wide
  assign and_9_out = _23 & _24 & _25 & _26;  // AND_Gate and_9, 2 bits wide
  assign and_10_out = _31 & _32 & _33 & _34;  // AND_Gate and_10, 2 bits wide
  assign and_11_out = _32 & _33 & _34 & _35;  // AND_Gate and_11, 2 bits wide
  assign and_12_out = _33 & _34 & _35 & _36;  // AND_Gate and_12, 2 bits wide
  assign and_13_out = _41 & _42 & _43 & _44;  // AND_Gate and_13, 2 bits wide
  assign and_14_out = _42 & _43 & _44 & _45;  // AND_Gate and_14, 2 bits wide
  assign and_15_out = _43 & _44 & _45 & _46;  // AND_Gate and_15, 2 bits wide
  assign and_16_out = _50 & _51 & _52 & _53;  // AND_Gate and_16, 2 bits wide
  assign and_17_out = _51 & _52 & _53 & _54;  // AND_Gate and_17, 2 bits wide
  assign and_18_out = _52 & _53 & _54 & _55;  // AND_Gate and_18, 2 bits wide
  assign and_19_out = _53 & _54 & _55 & _56;  // AND_Gate and_19, 2 bits wide
  assign and_20_out = _00 & _01 & _02 & _03;  // AND_Gate and_20, 2 bits wide
  assign or_1_out = and_20_out | and_1_out | and_2_out | and_3_out;  // OR_Gate or_1, 2 bits wide
  assign and_21_out = _10 & _11 & _12 & _13;  // AND_Gate and_21, 2 bits wide
  assign or_2_out = and_21_out | and_4_out | and_5_out | and_6_out;  // OR_Gate or_2, 2 bits wide
  assign and_22_out = _20 & _21 & _22 & _23;  // AND_Gate and_22, 2 bits wide
  assign or_3_out = and_22_out | and_7_out | and_8_out | and_9_out;  // OR_Gate or_3, 2 bits wide
  assign and_23_out = _30 & _31 & _32 & _33;  // AND_Gate and_23, 2 bits wide
  assign or_4_out = and_23_out | and_10_out | and_11_out | and_12_out;  // OR_Gate or_4, 2 bits wide
  assign and_24_out = _40 & _41 & _42 & _43;  // AND_Gate and_24, 2 bits wide
  assign or_5_out = and_24_out | and_13_out | and_14_out | and_15_out;  // OR_Gate or_5, 2 bits wide
  assign or_6_out = and_16_out | and_17_out | and_18_out | and_19_out;  // OR_Gate or_6, 2 bits wide
  Comparator #(.width(2), .mode("unsigned")) comparator_1 (
    .a(or_1_out), .b(2'b01), .eq(comparator_1_eq));  // open: gt, lt
  Comparator #(.width(2), .mode("unsigned")) comparator_2 (
    .a(or_1_out), .b(2'b10), .eq(comparator_2_eq));  // open: gt, lt
  Comparator #(.width(2), .mode("unsigned")) comparator_3 (
    .a(or_2_out), .b(2'b01), .eq(comparator_3_eq));  // open: gt, lt
  Comparator #(.width(2), .mode("unsigned")) comparator_4 (
    .a(or_2_out), .b(2'b10), .eq(comparator_4_eq));  // open: gt, lt
  Comparator #(.width(2), .mode("unsigned")) comparator_5 (
    .a(or_3_out), .b(2'b01), .eq(comparator_5_eq));  // open: gt, lt
  Comparator #(.width(2), .mode("unsigned")) comparator_6 (
    .a(or_3_out), .b(2'b10), .eq(comparator_6_eq));  // open: gt, lt
  Comparator #(.width(2), .mode("unsigned")) comparator_7 (
    .a(or_4_out), .b(2'b01), .eq(comparator_7_eq));  // open: gt, lt
  Comparator #(.width(2), .mode("unsigned")) comparator_8 (
    .a(or_4_out), .b(2'b10), .eq(comparator_8_eq));  // open: gt, lt
  Comparator #(.width(2), .mode("unsigned")) comparator_9 (
    .a(or_5_out), .b(2'b01), .eq(comparator_9_eq));  // open: gt, lt
  Comparator #(.width(2), .mode("unsigned")) comparator_10 (
    .a(or_5_out), .b(2'b10), .eq(comparator_10_eq));  // open: gt, lt
  Comparator #(.width(2), .mode("unsigned")) comparator_11 (
    .a(or_6_out), .b(2'b01), .eq(comparator_11_eq));  // open: gt, lt
  or or_7 (or_7_out, comparator_11_eq, comparator_12_eq);
  Comparator #(.width(2), .mode("unsigned")) comparator_12 (
    .a(or_6_out), .b(2'b10), .eq(comparator_12_eq));  // open: gt, lt
  or or_8 (or_8_out, comparator_1_eq, comparator_2_eq);
  or or_9 (or_9_out, comparator_3_eq, comparator_4_eq);
  or or_10 (or_10_out, comparator_5_eq, comparator_6_eq);
  or or_11 (or_11_out, comparator_7_eq, comparator_8_eq);
  or or_12 (or_12_out, comparator_9_eq, comparator_10_eq);
  or or_13 (out_43, or_8_out, or_9_out, or_10_out, or_11_out, or_12_out, or_7_out);
endmodule

module Diagonal (
  input  [1:0] _00,
  input  [1:0] _20,
  input  [1:0] _40,
  input  [1:0] _01,
  input  [1:0] _21,
  input  [1:0] _41,
  input  [1:0] _02,
  input  [1:0] _22,
  input  [1:0] _42,
  input  [1:0] _03,
  input  [1:0] _23,
  input  [1:0] _43,
  input  [1:0] _04,
  input  [1:0] _24,
  input  [1:0] _44,
  input  [1:0] _05,
  input  [1:0] _25,
  input  [1:0] _45,
  input  [1:0] _06,
  input  [1:0] _26,
  input  [1:0] _46,
  input  [1:0] _10,
  input  [1:0] _30,
  input  [1:0] _50,
  input  [1:0] _11,
  input  [1:0] _31,
  input  [1:0] _51,
  input  [1:0] _12,
  input  [1:0] _32,
  input  [1:0] _52,
  input  [1:0] _13,
  input  [1:0] _33,
  input  [1:0] _53,
  input  [1:0] _14,
  input  [1:0] _34,
  input  [1:0] _54,
  input  [1:0] _15,
  input  [1:0] _35,
  input  [1:0] _55,
  input  [1:0] _16,
  input  [1:0] _36,
  input  [1:0] _56,
  output out_43
);

  wire comparator_1_eq, comparator_2_eq, comparator_3_eq, comparator_4_eq, comparator_5_eq, comparator_6_eq,
       comparator_7_eq, comparator_8_eq, comparator_9_eq, comparator_10_eq, comparator_11_eq,
       comparator_12_eq, comparator_13_eq, comparator_14_eq, comparator_15_eq, comparator_16_eq,
       comparator_17_eq, comparator_18_eq, comparator_19_eq, comparator_20_eq, comparator_21_eq,
       comparator_22_eq, comparator_23_eq, comparator_24_eq, d_i, i_d, or_5_out, or_6_out, or_7_out,
       or_8_out, or_9_out, or_10_out, or_17_out, or_18_out, or_19_out, or_20_out, or_21_out, or_22_out;
  wire [1:0] and_1_out, and_2_out, and_3_out, and_4_out, and_5_out, and_6_out, and_7_out, and_8_out,
       and_9_out, and_10_out, and_11_out, and_12_out, and_13_out, and_14_out, and_15_out, and_16_out,
       and_17_out, and_18_out, and_19_out, and_20_out, and_21_out, and_22_out, and_23_out, and_24_out,
       or_1_out, or_2_out, or_3_out, or_4_out, or_13_out, or_14_out, or_15_out, or_16_out;

  assign and_1_out = _20 & _31 & _42 & _53;  // AND_Gate and_1, 2 bits wide
  assign and_2_out = _03 & _14 & _25 & _36;  // AND_Gate and_2, 2 bits wide
  assign and_3_out = _00 & _11 & _22 & _33;  // AND_Gate and_3, 2 bits wide
  assign and_4_out = _11 & _22 & _33 & _44;  // AND_Gate and_4, 2 bits wide
  assign and_5_out = _22 & _33 & _44 & _55;  // AND_Gate and_5, 2 bits wide
  assign and_6_out = _10 & _21 & _32 & _43;  // AND_Gate and_6, 2 bits wide
  assign and_7_out = _21 & _32 & _43 & _54;  // AND_Gate and_7, 2 bits wide
  assign and_8_out = _01 & _12 & _23 & _34;  // AND_Gate and_8, 2 bits wide
  assign and_9_out = _12 & _23 & _34 & _45;  // AND_Gate and_9, 2 bits wide
  assign and_10_out = _23 & _34 & _45 & _56;  // AND_Gate and_10, 2 bits wide
  assign and_11_out = _02 & _13 & _24 & _35;  // AND_Gate and_11, 2 bits wide
  assign and_12_out = _13 & _24 & _35 & _46;  // AND_Gate and_12, 2 bits wide
  assign or_1_out = and_3_out | and_4_out | and_5_out;  // OR_Gate or_1, 2 bits wide
  assign or_2_out = and_6_out | and_7_out;  // OR_Gate or_2, 2 bits wide
  assign or_3_out = and_8_out | and_9_out | and_10_out;  // OR_Gate or_3, 2 bits wide
  assign or_4_out = and_11_out | and_12_out;  // OR_Gate or_4, 2 bits wide
  Comparator #(.width(2), .mode("unsigned")) comparator_1 (
    .a(or_1_out), .b(2'b01), .eq(comparator_1_eq));  // open: gt, lt
  Comparator #(.width(2), .mode("unsigned")) comparator_2 (
    .a(or_1_out), .b(2'b10), .eq(comparator_2_eq));  // open: gt, lt
  Comparator #(.width(2), .mode("unsigned")) comparator_3 (
    .a(or_2_out), .b(2'b01), .eq(comparator_3_eq));  // open: gt, lt
  Comparator #(.width(2), .mode("unsigned")) comparator_4 (
    .a(or_2_out), .b(2'b10), .eq(comparator_4_eq));  // open: gt, lt
  Comparator #(.width(2), .mode("unsigned")) comparator_5 (
    .a(and_1_out), .b(2'b01), .eq(comparator_5_eq));  // open: gt, lt
  Comparator #(.width(2), .mode("unsigned")) comparator_6 (
    .a(and_1_out), .b(2'b10), .eq(comparator_6_eq));  // open: gt, lt
  Comparator #(.width(2), .mode("unsigned")) comparator_7 (
    .a(or_3_out), .b(2'b01), .eq(comparator_7_eq));  // open: gt, lt
  Comparator #(.width(2), .mode("unsigned")) comparator_8 (
    .a(or_3_out), .b(2'b10), .eq(comparator_8_eq));  // open: gt, lt
  Comparator #(.width(2), .mode("unsigned")) comparator_9 (
    .a(or_4_out), .b(2'b01), .eq(comparator_9_eq));  // open: gt, lt
  Comparator #(.width(2), .mode("unsigned")) comparator_10 (
    .a(or_4_out), .b(2'b10), .eq(comparator_10_eq));  // open: gt, lt
  Comparator #(.width(2), .mode("unsigned")) comparator_11 (
    .a(and_2_out), .b(2'b01), .eq(comparator_11_eq));  // open: gt, lt
  Comparator #(.width(2), .mode("unsigned")) comparator_12 (
    .a(and_2_out), .b(2'b10), .eq(comparator_12_eq));  // open: gt, lt
  or or_5 (or_5_out, comparator_1_eq, comparator_2_eq);
  or or_6 (or_6_out, comparator_3_eq, comparator_4_eq);
  or or_7 (or_7_out, comparator_5_eq, comparator_6_eq);
  or or_8 (or_8_out, comparator_7_eq, comparator_8_eq);
  or or_9 (or_9_out, comparator_9_eq, comparator_10_eq);
  or or_10 (or_10_out, comparator_11_eq, comparator_12_eq);
  or or_11 (i_d, or_5_out, or_6_out, or_7_out, or_8_out, or_9_out, or_10_out);
  or or_12 (out_43, i_d, d_i);
  assign and_13_out = _26 & _35 & _44 & _53;  // AND_Gate and_13, 2 bits wide
  assign and_14_out = _03 & _12 & _21 & _30;  // AND_Gate and_14, 2 bits wide
  assign and_15_out = _06 & _15 & _24 & _33;  // AND_Gate and_15, 2 bits wide
  assign and_16_out = _15 & _24 & _33 & _42;  // AND_Gate and_16, 2 bits wide
  assign and_17_out = _24 & _33 & _42 & _51;  // AND_Gate and_17, 2 bits wide
  assign and_18_out = _16 & _25 & _34 & _43;  // AND_Gate and_18, 2 bits wide
  assign and_19_out = _25 & _34 & _43 & _52;  // AND_Gate and_19, 2 bits wide
  assign and_20_out = _05 & _14 & _23 & _32;  // AND_Gate and_20, 2 bits wide
  assign and_21_out = _14 & _23 & _32 & _41;  // AND_Gate and_21, 2 bits wide
  assign and_22_out = _23 & _32 & _41 & _50;  // AND_Gate and_22, 2 bits wide
  assign and_23_out = _04 & _13 & _22 & _31;  // AND_Gate and_23, 2 bits wide
  assign and_24_out = _13 & _22 & _31 & _40;  // AND_Gate and_24, 2 bits wide
  assign or_13_out = and_15_out | and_16_out | and_17_out;  // OR_Gate or_13, 2 bits wide
  assign or_14_out = and_18_out | and_19_out;  // OR_Gate or_14, 2 bits wide
  assign or_15_out = and_20_out | and_21_out | and_22_out;  // OR_Gate or_15, 2 bits wide
  assign or_16_out = and_23_out | and_24_out;  // OR_Gate or_16, 2 bits wide
  Comparator #(.width(2), .mode("unsigned")) comparator_13 (
    .a(or_13_out), .b(2'b01), .eq(comparator_13_eq));  // open: gt, lt
  Comparator #(.width(2), .mode("unsigned")) comparator_14 (
    .a(or_13_out), .b(2'b10), .eq(comparator_14_eq));  // open: gt, lt
  Comparator #(.width(2), .mode("unsigned")) comparator_15 (
    .a(or_14_out), .b(2'b01), .eq(comparator_15_eq));  // open: gt, lt
  Comparator #(.width(2), .mode("unsigned")) comparator_16 (
    .a(or_14_out), .b(2'b10), .eq(comparator_16_eq));  // open: gt, lt
  Comparator #(.width(2), .mode("unsigned")) comparator_17 (
    .a(and_13_out), .b(2'b01), .eq(comparator_17_eq));  // open: gt, lt
  Comparator #(.width(2), .mode("unsigned")) comparator_18 (
    .a(and_13_out), .b(2'b10), .eq(comparator_18_eq));  // open: gt, lt
  Comparator #(.width(2), .mode("unsigned")) comparator_19 (
    .a(or_15_out), .b(2'b01), .eq(comparator_19_eq));  // open: gt, lt
  Comparator #(.width(2), .mode("unsigned")) comparator_20 (
    .a(or_15_out), .b(2'b10), .eq(comparator_20_eq));  // open: gt, lt
  Comparator #(.width(2), .mode("unsigned")) comparator_21 (
    .a(or_16_out), .b(2'b01), .eq(comparator_21_eq));  // open: gt, lt
  Comparator #(.width(2), .mode("unsigned")) comparator_22 (
    .a(or_16_out), .b(2'b10), .eq(comparator_22_eq));  // open: gt, lt
  Comparator #(.width(2), .mode("unsigned")) comparator_23 (
    .a(and_14_out), .b(2'b01), .eq(comparator_23_eq));  // open: gt, lt
  Comparator #(.width(2), .mode("unsigned")) comparator_24 (
    .a(and_14_out), .b(2'b10), .eq(comparator_24_eq));  // open: gt, lt
  or or_17 (or_17_out, comparator_13_eq, comparator_14_eq);
  or or_18 (or_18_out, comparator_15_eq, comparator_16_eq);
  or or_19 (or_19_out, comparator_17_eq, comparator_18_eq);
  or or_20 (or_20_out, comparator_19_eq, comparator_20_eq);
  or or_21 (or_21_out, comparator_21_eq, comparator_22_eq);
  or or_22 (or_22_out, comparator_23_eq, comparator_24_eq);
  or or_23 (d_i, or_17_out, or_18_out, or_19_out, or_20_out, or_21_out, or_22_out);
endmodule

module Turno (
  input  c1,
  input  c2,
  input  c3,
  input  c4,
  input  c5,
  input  c6,
  input  c7,
  input  [6:0] l1,
  output [1:0] Jugador,
  output Invalida
);

  wire and_1_out, and_2_out, and_3_out, and_4_out, and_5_out, and_6_out, and_7_out, and_8_out, and_9_out,
       and_10_out, and_11_out, and_12_out, and_13_out, and_14_out, counter_1_carry, not_1_out, not_2_out,
       not_3_out, not_4_out, not_5_out, not_6_out, not_7_out, or_2_out;

  Counter #(.width(2), .max('h2)) counter_1 (
    .load(counter_1_carry), .D(2'b01), .Q(Jugador), .carry(counter_1_carry), .clk(or_2_out));  // open: count, clr, preset, down
  and and_1 (and_1_out, c1, l1[0]);
  not not_1 (not_1_out, l1[0]);
  and and_2 (and_2_out, c1, not_1_out);
  and and_3 (and_3_out, c2, l1[1]);
  not not_2 (not_2_out, l1[1]);
  and and_4 (and_4_out, c2, not_2_out);
  and and_5 (and_5_out, c3, l1[2]);
  not not_3 (not_3_out, l1[2]);
  and and_6 (and_6_out, c3, not_3_out);
  or or_1 (Invalida, and_1_out, and_3_out, and_5_out, and_7_out, and_9_out, and_11_out, and_13_out);
  and and_7 (and_7_out, c4, l1[3]);
  not not_4 (not_4_out, l1[3]);
  and and_8 (and_8_out, c4, not_4_out);
  or or_2 (or_2_out, and_2_out, and_4_out, and_6_out, and_8_out, and_10_out, and_12_out, and_14_out);
  and and_9 (and_9_out, c5, l1[4]);
  not not_5 (not_5_out, l1[4]);
  and and_10 (and_10_out, c5, not_5_out);
  and and_11 (and_11_out, c6, l1[5]);
  not not_6 (not_6_out, l1[5]);
  and and_12 (and_12_out, c6, not_6_out);
  and and_13 (and_13_out, c7, l1[6]);
  not not_7 (not_7_out, l1[6]);
  and and_14 (and_14_out, c7, not_7_out);

  // Other names for the same wires on the sheet: f1 = l1[0]; f2 = l1[1]; f3 = l1[2]; f4 = l1[3]; f5 = l1[4];
  //   f6 = l1[5]; f7 = l1[6]
endmodule

module Color (
  input  [1:0] Jugador,
  output [23:0] out_2
);

  Multiplexer #(.select(2), .width(24), .enable("false")) multiplexer_1 (
    .in0(24'h808080), .in1(24'h6a0dad), .in2(24'hff00), .out(out_2), .sel(Jugador));  // open: in3
endmodule

module pantalla (
  input  Invalida,
  input  Clear,
  input  [1:0] Jugador,
  input  Gana,
  output Lock,
  output [6:0] valor,
  output entrada,
  output parar
);

  wire and_1_out, and_2_out, and_3_out, Clock, counter_2_carry, counter_3_carry, counter_4_carry, not_1_out,
       not_2_out, Reset;
  wire [1:1] counter_1_q;
  wire [5:0] counter_2_q, counter_4_q;
  wire [6:0] adder_1_out, bit_extender_1_out, multiplexer_1_out, rom_1_data, rom_2_data;

  Clock clock_1 (.out(Clock));
  Counter #(.width(2), .max('h2)) counter_1 (
    .Q({counter_1_q[1], Lock}), .clk(Invalida), .clr(Reset));  // open: load, D, count, carry, preset, down
  assign bit_extender_1_out = {{5{1'b0}}, Jugador};  // Bit_Extender bit_extender_1
  and and_1 (and_1_out, Gana, not_1_out);
  not not_1 (not_1_out, counter_3_carry);
  Adder #(.width(7)) adder_1 (.a(bit_extender_1_out), .b(7'b0110000), .out(adder_1_out));  // open: cin, cout
  and and_2 (and_2_out, Clock, and_1_out);
  Multiplexer #(.width(7), .enable("false")) multiplexer_1 (
    .in0(rom_1_data), .in1(adder_1_out), .out(multiplexer_1_out), .sel(counter_2_carry));
  Counter #(.width(6), .max('h16)) counter_2 (
    .count(not_2_out), .Q(counter_2_q), .carry(counter_2_carry), .clk(and_2_out), .clr(Clear));  // open: load, D, preset, down
  not not_2 (not_2_out, counter_2_carry);
  Multiplexer #(.width(7), .enable("false")) multiplexer_2 (
    .in0(multiplexer_1_out), .in1(rom_2_data), .out(valor), .sel(Lock));
  ROM #(.addrWidth(6), .dataWidth(7), .Select("low")) rom_1 (.addr(counter_2_q), .data(rom_1_data));
  and and_3 (and_3_out, Clock, Lock);
  Counter #(.width(6), .max('h17)) counter_3 (
    .count(parar), .carry(counter_3_carry), .clk(and_2_out), .clr(Clear));  // open: load, D, Q, preset, down
  Counter #(.width(6), .max('h13)) counter_4 (
    .Q(counter_4_q), .carry(counter_4_carry), .clk(and_3_out), .clr(Reset));  // open: load, D, count, preset, down
  or or_1 (Reset, counter_4_carry, Clear);
  or or_2 (entrada, and_3_out, and_2_out);
  not not_3 (parar, counter_3_carry);
  ROM #(.addrWidth(6), .dataWidth(7), .Select("low")) rom_2 (.addr(counter_4_q), .data(rom_2_data));

  // Other names for the same wires on the sheet: Invalida_t = Lock

  // Notes on the sheet:
  //   contents of rom_1 (hex, n*v repeats v):
  //   20 48 61 20 67 61 6e 61 64 6f 20 65 6c 20 6a 75 67 61 64 6f 72 3a 20
  //   contents of rom_2 (hex, n*v repeats v):
  //   20 4a 75 67 61 64 61 20 69 6e 76 61 6c 69 64 61 4*2e
endmodule
